# Fritzing sketch Scheme (saved by Fritzing 0.9.4)

parts:
  Компонент1 = Logic Level Converter
  Компонент2 = Arduino Uno (Rev3)
  Raspberry_Pi_1 = Raspberry Pi 3 [part_number=RPI-3-V1.2]

nets:
  N1: Компонент1.TX2_LV, Raspberry_Pi_1.GIPO8
  N2: Компонент1.RX2_LV, Raspberry_Pi_1.GIPO11
  GND: Компонент1.GND, Компонент2.GND, Raspberry_Pi_1.GND
  N3: Компонент1.LV, Raspberry_Pi_1.3V3
  N4: Компонент1.RX_LV, Raspberry_Pi_1.GIPO9
  N5: Компонент1.TX_LV, Raspberry_Pi_1.GIPO10
  N6: Компонент1.TX_HV, Компонент2.D11_PWM/MOSI
  N7: Компонент1.RX_HV, Компонент2.D12/MISO
  N8: Компонент1.HV, Компонент2.5V
  N9: Компонент1.RX2_HV, Компонент2.D13/SCK
  N10: Компонент1.TX2_HV, Компонент2.D10_PWM/SS
